# Fritzing sketch LDR_GreenRed_LED (saved by Fritzing 0.9.9b)
breadboards: 1

parts:
  WeMos_D1_Mini1 = WeMos D1 Mini  # not connected
  LED1 = LED - 5mm [color="Green (570nm)" current=0.030 package="5 mm [THT]"]
  LED2 = LED - 5mm [color="Red (633nm)" current=0.030 package="5 mm [THT]"]
  R1 = Resistor [tolerance=±5% power=0.25 resistance=220 package=THT]
  R2 = Resistor [tolerance=±5% power=0.25 resistance=220 package=THT]
  R4 = Resistor [tolerance=±5% power=0.25 resistance=10k package=THT]
  R5 = Photocell (LDR) [package=THT]

nets:
  N1: LED1.cathode, R1.Pin_1
  N2: LED2.cathode, R2.Pin_1
  N3: R1.Pin_0, R2.Pin_0, R4.Pin_0
  N4: R4.Pin_1, R5.pin_1
